// Logisim project alu.circ as structural Verilog: 3 circuits, main circuit alu
module alu (
  input  [31:0] A,
  input  [31:0] B,
  input  [3:0] ALUSel,
  output [31:0] Result
);

  wire comparator_1_lt, comparator_2_eq;
  wire [6:0] bitadder_1_out;
  wire [31:0] Add_res, And_res, Cnto_res, Div_res, Divu_res, Mulh_res, Mulhu_res, Mult_res, Or_res, Remu_res,
       Sir_res, Sll_res, Slt_res, Sra_res, Srl_res, Sub_res, Xor_res;

  Divider #(.width(32)) divider_1 (.a(A), .b(B), .out(Divu_res), .rem(Remu_res));  // open: upper
  Shifter #(.width(32), .shift("lr")) shifter_1 (.in(A), .\dist (B[4:0]), .out(Srl_res));
  Shifter #(.width(32), .shift("ar")) shifter_2 (.in(A), .\dist (B[4:0]), .out(Sra_res));
  Comparator #(.width(32)) comparator_1 (.a(A), .b(B), .lt(comparator_1_lt));  // open: gt, eq
  Shifter #(.width(32)) shifter_3 (.in(A), .\dist (B[4:0]), .out(Sll_res));
  assign Slt_res = {{31{1'b0}}, comparator_1_lt};  // Bit_Extender bit_extender_1
  assign And_res = A & B;  // AND_Gate and_1, 32 bits wide
  assign Or_res = A | B;  // OR_Gate or_1, 32 bits wide
  assign Xor_res = A ^ B;  // XOR_Gate xor_1, 32 bits wide
  Adder #(.width(32)) adder_1 (.a(A), .b(B), .out(Add_res));  // open: cin, cout
  Subtractor #(.width(32)) subtractor_1 (.a(A), .b(B), .out(Sub_res));  // open: bin, bout
  Multiplier #(.width(32)) multiplier_1 (.a(A), .b(B), .out(Mult_res), .cout(Mulhu_res));  // open: cin
  Mulh mulh_1 (.in_1(A), .in_2(B), .out_3(Mulh_res));
  Div div_1 (.in_1(A), .in_2(B), .out_3(Div_res));
  BitAdder #(.width(32)) bitadder_1 (.in0(A), .in1(B), .out(bitadder_1_out));
  assign Cnto_res = {{25{1'b0}}, bitadder_1_out};  // Bit_Extender bit_extender_2
  Comparator #(.width(32)) comparator_2 (
    .a(A),
    .b({B[0], B[1], B[2], B[3], B[4], B[5], B[6], B[7], B[8], B[9], B[10], B[11], B[12], B[13], B[14], B[15], B[16], B[17], B[18], B[19], B[20], B[21], B[22], B[23], B[24], B[25], B[26], B[27], B[28], B[29], B[30], B[31]}),
    .eq(comparator_2_eq));  // open: gt, lt
  assign Sir_res = {{31{1'b0}}, comparator_2_eq};  // Bit_Extender bit_extender_3
  Multiplexer #(.select(4), .width(32), .enable("false")) multiplexer_1 (
    .in0(And_res), .in1(Or_res), .in2(Xor_res), .in3(Add_res), .in4(Sub_res), .in5(Mult_res),
    .in6(Mulhu_res), .in7(Mulh_res), .in8(Divu_res), .in9(Div_res), .in10(Remu_res), .in11(Srl_res),
    .in12(Sra_res), .in13(Slt_res), .in14(Sir_res), .in15(Sll_res), .out(Result), .sel(ALUSel));

  // Notes on the sheet:
  //   INPUTS to your circuit
  //   DON'T CHANGE THE LOCATIONS OF THE INPUTS AND OUTPUTS!
  //   Implemention of ALU
  //   OUTPUT from your circuit
endmodule

module Mulh (
  input  [31:0] in_1,
  input  [31:0] in_2,
  output [31:0] out_3
);

  wire xnor_1_out;
  wire [0:0] comparator_1_eq;
  wire [31:0] adder_1_out, multiplexer_1_out, multiplexer_2_out, multiplier_1_cout, multiplier_1_out,
       negator_1_out, negator_2_out, not_1_out;

  Negator #(.width(32)) negator_1 (.in(in_1), .out(negator_1_out));
  Negator #(.width(32)) negator_2 (.in(in_2), .out(negator_2_out));
  Multiplexer #(.width(32), .enable("false")) multiplexer_1 (
    .in0(in_1), .in1(negator_1_out), .out(multiplexer_1_out), .sel(in_1[31]));
  Multiplexer #(.width(32), .enable("false")) multiplexer_2 (
    .in0(in_2), .in1(negator_2_out), .out(multiplexer_2_out), .sel(in_2[31]));
  Multiplier #(.width(32)) multiplier_1 (
    .a(multiplexer_1_out), .b(multiplexer_2_out), .out(multiplier_1_out), .cout(multiplier_1_cout));  // open: cin
  xnor xnor_1 (xnor_1_out, in_1[31], in_2[31]);
  Comparator #(.width(32)) comparator_1 (
    .a(multiplier_1_out), .b({32{1'b0}}), .eq(comparator_1_eq[0]));  // open: gt, lt
  assign not_1_out = ~multiplier_1_cout;  // NOT_Gate not_1, 32 bits wide
  Adder #(.width(32)) adder_1 (
    .a({{31{1'b0}}, comparator_1_eq[0]}), .b(not_1_out), .out(adder_1_out));  // open: cin, cout
  Multiplexer #(.width(32), .enable("false")) multiplexer_3 (
    .in0(adder_1_out), .in1(multiplier_1_cout), .out(out_3), .sel(xnor_1_out));
endmodule

module Div (
  input  [31:0] in_1,
  input  [31:0] in_2,
  output [31:0] out_3
);

  wire xor_1_out;
  wire [31:0] divider_1_out, multiplexer_1_out, multiplexer_2_out, negator_1_out, negator_2_out,
       negator_3_out;

  Negator #(.width(32)) negator_1 (.in(in_1), .out(negator_1_out));
  Negator #(.width(32)) negator_2 (.in(in_2), .out(negator_2_out));
  Multiplexer #(.width(32), .enable("false")) multiplexer_1 (
    .in0(in_1), .in1(negator_1_out), .out(multiplexer_1_out), .sel(in_1[31]));
  Multiplexer #(.width(32), .enable("false")) multiplexer_2 (
    .in0(in_2), .in1(negator_2_out), .out(multiplexer_2_out), .sel(in_2[31]));
  Divider #(.width(32)) divider_1 (
    .a(multiplexer_1_out), .b(multiplexer_2_out), .out(divider_1_out));  // open: upper, rem
  xor xor_1 (xor_1_out, in_1[31], in_2[31]);
  Negator #(.width(32)) negator_3 (.in(divider_1_out), .out(negator_3_out));
  Multiplexer #(.width(32), .enable("false")) multiplexer_3 (
    .in0(divider_1_out), .in1(negator_3_out), .out(out_3), .sel(xor_1_out));
endmodule
