// Logisim project cpu.circ as structural Verilog: 4 circuits, main circuit main
module main (
  input  [31:0] INSTRUCTION,
  input  CLOCK,
  output [31:0] FETCH_ADDRESS,
  output [31:0] ra,
  output [31:0] sp,
  output [31:0] t0,
  output [31:0] t1,
  output [31:0] t2,
  output [31:0] s0,
  output [31:0] s1,
  output [31:0] a0
);

  wire B_Sel, BrEq, BrLt, BrUn, MemWEn, PCSel, RegWEn;
  wire [1:0] A_Sel, WBSel;
  wire [2:0] ImmSel, Mem_Read_Sel;
  wire [3:0] Alu_Sel;
  wire [31:0] A, adder_1_out, alu_res, B, bit_extender_1_out, bit_extender_2_out, bit_extender_3_out,
       bit_extender_4_out, Immediate, instruction_t, Mem_Read_Data, multiplexer_1_out, multiplexer_2_out, PC,
       PC_plus4, R1, R2, Read_Data, shifter_1_out, shifter_2_out, Write_Data;

  Shifter #(.width(32), .shift("lr")) shifter_1 (.in(alu_res), .\dist (5'b00010), .out(shifter_1_out));
  Adder #(.width(32)) adder_1 (.a(FETCH_ADDRESS), .b(32'h1), .out(adder_1_out));  // open: cin, cout
  Multiplexer #(.width(32), .enable("false")) multiplexer_1 (
    .in0(adder_1_out), .in1(shifter_1_out), .out(multiplexer_1_out), .sel(PCSel));
  Register #(.width(32)) u_PC (.D(multiplexer_1_out), .clk(CLOCK), .Q(FETCH_ADDRESS));  // open: en, clr
  Multiplexer #(.width(32), .enable("false")) multiplexer_2 (
    .in0(INSTRUCTION), .in1(32'h13), .out(multiplexer_2_out), .sel(PCSel));
  imm_gen imm_gen_1 (.Instruction(instruction_t), .Imm_sel(ImmSel), .Immediate(Immediate));
  Shifter #(.width(32)) shifter_2 (.in(FETCH_ADDRESS), .\dist (5'b00010), .out(shifter_2_out));
  Register #(.width(32)) register_1 (.D(multiplexer_2_out), .clk(CLOCK), .Q(instruction_t));  // open: en, clr
  Register #(.width(32)) register_2 (.D(shifter_2_out), .clk(CLOCK), .Q(PC));  // open: en, clr
  Control control_1 (
    .Instruction(instruction_t), .BrEq(BrEq), .BrLt(BrLt), .BrUn(BrUn), .PCSel(PCSel), .ImmSel(ImmSel),
    .MemRw(MemWEn), .RegWEn(RegWEn), .WBSel(WBSel), .B_Sel(B_Sel), .A_Sel(A_Sel),
    .Mem_Read_Sel(Mem_Read_Sel), .Alu_Sel(Alu_Sel));
  Multiplexer #(.select(2), .width(32), .enable("false")) multiplexer_3 (
    .in0(R1), .in1(PC), .in2({32{1'b0}}), .out(A), .sel(A_Sel));  // open: in3
  Multiplexer #(.width(32), .enable("false")) multiplexer_4 (.in0(R2), .in1(Immediate), .out(B), .sel(B_Sel));
  Branch_Compare branch_compare_1 (.reg1(R1), .reg2(R2), .BrUn(BrUn), .BrEq(BrEq), .BrLt(BrLt));
  regfile_main RegFile (
    .rs2(instruction_t[24:20]), .rd(instruction_t[11:7]), .Read_Data_1(R1), .Read_Data_2(R2), .ra(ra),
    .sp(sp), .t0(t0), .t1(t1), .t2(t2), .s0(s0), .s1(s1), .a0(a0), .rs1(instruction_t[19:15]),
    .Write_Data(Write_Data), .RegWEn(RegWEn), .clk(CLOCK));
  Adder #(.width(32)) adder_2 (.a(PC), .b(32'h4), .out(PC_plus4));  // open: cin, cout
  alu Arithmetic_Logic_Unit (.A(A), .B(B), .ALUSel(Alu_Sel), .Result(alu_res));
  assign bit_extender_1_out = {{24{Read_Data[7]}}, Read_Data[7:0]};  // Bit_Extender bit_extender_1
  assign bit_extender_2_out = {{16{Read_Data[15]}}, Read_Data[15:0]};  // Bit_Extender bit_extender_2
  assign bit_extender_3_out = {{24{1'b0}}, Read_Data[7:0]};  // Bit_Extender bit_extender_3
  assign bit_extender_4_out = {{16{1'b0}}, Read_Data[15:0]};  // Bit_Extender bit_extender_4
  Multiplexer #(.select(2), .width(32), .enable("false")) multiplexer_5 (
    .in0(Mem_Read_Data), .in1(alu_res), .in2(PC_plus4), .out(Write_Data), .sel(WBSel));  // open: in3
  mem_main DMEM (.Address(alu_res), .Write_en(MemWEn), .clk(CLOCK), .Write_data(R2), .Read_data(Read_Data));
  Multiplexer #(.select(3), .width(32), .enable("false")) multiplexer_6 (
    .in0(bit_extender_1_out), .in1(bit_extender_2_out), .in2(Read_Data), .in3(bit_extender_3_out),
    .in4(bit_extender_4_out), .out(Mem_Read_Data), .sel(Mem_Read_Sel));  // open: in5, in6, in7

  // Other names for the same wires on the sheet: clk = CLOCK; fetch_addr[31:0] = FETCH_ADDRESS;
  //   rd[4:0] = instruction_t[11:7]; rs1[4:0] = instruction_t[19:15]; rs2[4:0] = instruction_t[24:20]

  // Notes on the sheet:
  //   Output
  //   Inputs/Outputs from run.circ. DO NOT MOVE THESE.
  //   Inputs
  //   Inputs/Outputs from run.circ. DO NOT MOVE THESE.
endmodule

module imm_gen (
  input  [31:0] Instruction,
  input  [2:0] Imm_sel,
  output [31:0] Immediate
);

  wire [31:0] bit_extender_1_out, bit_extender_2_out, bit_extender_3_out, bit_extender_4_out;

  assign bit_extender_1_out = {{20{Instruction[31]}}, Instruction[31:20]};  // Bit_Extender bit_extender_1
  assign bit_extender_2_out = {{20{Instruction[31]}}, {Instruction[31:25], Instruction[11:7]}};  // Bit_Extender bit_extender_2
  assign bit_extender_3_out = {{19{Instruction[31]}}, {Instruction[31], Instruction[7], Instruction[30:25], Instruction[11:8], 1'b0}};  // Bit_Extender bit_extender_3
  assign bit_extender_4_out = {{11{Instruction[31]}}, {Instruction[31], Instruction[19:12], Instruction[20], Instruction[30:21], 1'b0}};  // Bit_Extender bit_extender_4
  Multiplexer #(.select(3), .width(32), .enable("false")) multiplexer_1 (
    .in0(bit_extender_1_out), .in1(bit_extender_2_out), .in2(bit_extender_3_out),
    .in3({Instruction[31:12], {12{1'b0}}}), .in4(bit_extender_4_out), .out(Immediate), .sel(Imm_sel));  // open: in5, in6, in7

  // Notes on the sheet:
  //   I-type
  //   S-type
  //   B-type
  //   U-type
  //   J-type
endmodule

module Branch_Compare (
  input  [31:0] reg1,
  input  [31:0] reg2,
  input  BrUn,
  output BrEq,
  output BrLt
);

  wire comparator_1_eq, comparator_1_lt, comparator_2_eq, comparator_2_lt;

  Comparator #(.width(32)) comparator_1 (.a(reg1), .b(reg2), .eq(comparator_1_eq), .lt(comparator_1_lt));  // open: gt
  Comparator #(.width(32), .mode("unsigned")) comparator_2 (
    .a(reg1), .b(reg2), .eq(comparator_2_eq), .lt(comparator_2_lt));  // open: gt
  Multiplexer #(.enable("false")) multiplexer_1 (.in0(comparator_1_eq), .in1(comparator_2_eq), .out(BrEq), .sel(BrUn));
  Multiplexer #(.enable("false")) multiplexer_2 (.in0(comparator_1_lt), .in1(comparator_2_lt), .out(BrLt), .sel(BrUn));
endmodule

module Control (
  input  [31:0] Instruction,
  input  BrEq,
  input  BrLt,
  output BrUn,
  output PCSel,
  output [2:0] ImmSel,
  output MemRw,
  output RegWEn,
  output [1:0] WBSel,
  output B_Sel,
  output [1:0] A_Sel,
  output [2:0] Mem_Read_Sel,
  output [3:0] Alu_Sel
);

  wire and_1_out, and_2_out, and_3_out, and_4_out, and_5_out, func3_0, func3_1, func3_2, func3_3, func3_4,
       func3_5, func3_6, func3_7, func7_00, func7_01, func7_20, I_addi, I_andi, I_imm_type, I_jalr, I_lb,
       I_lbu, I_lh, I_lhu, I_load_type, I_lw, I_ori, I_slli, I_slti, I_srli, I_type, I_xori, not_1_out,
       not_2_out, or_1_out, or_2_out, or_4_out, or_6_out, or_7_out, or_8_out, or_10_out, or_11_out,
       or_12_out, or_13_out, or_14_out, R_add, R_and, R_div, R_divu, R_mul, R_mulh, R_mulhu, R_or, R_remu,
       R_sll, R_srl, R_sub, R_type, R_xor, S_sw, SB_beq, SB_bgeu, SB_blt, SB_bltu, SB_bne, SB_type, U_auipc,
       U_lui, UJ_jal;
  wire [1:0] multiplexer_14_out, multiplexer_22_out;
  wire [2:0] multiplexer_1_out, multiplexer_3_out, multiplexer_5_out, multiplexer_7_out, multiplexer_20_out,
       multiplexer_23_out, multiplexer_25_out, multiplexer_26_out;
  wire [3:0] multiplexer_2_out, multiplexer_4_out, multiplexer_6_out, multiplexer_8_out, multiplexer_10_out,
       multiplexer_11_out, multiplexer_12_out, multiplexer_13_out, multiplexer_15_out, multiplexer_17_out,
       multiplexer_18_out, multiplexer_19_out;

  not not_1 (not_1_out, BrEq);
  not not_2 (not_2_out, BrLt);
  Multiplexer #(.width(3), .enable("false")) multiplexer_1 (
    .in0(3'b000), .in1(3'b000), .out(multiplexer_1_out), .sel(or_1_out));
  or or_1 (or_1_out, R_type, I_type);
  Multiplexer #(.width(4), .enable("false")) multiplexer_2 (
    .in0(4'b0000), .in1(4'b0001), .out(multiplexer_2_out), .sel(or_2_out));
  or or_2 (or_2_out, R_or, I_ori);
  and and_1 (and_1_out, SB_beq, BrEq);
  and and_2 (and_2_out, SB_bltu, BrLt);
  and and_3 (and_3_out, SB_bne, not_1_out);
  and and_4 (and_4_out, SB_blt, BrLt);
  and and_5 (and_5_out, SB_bgeu, not_2_out);
  or or_3 (I_type, I_load_type, I_imm_type, I_jalr);
  or or_4 (or_4_out, R_xor, I_xori);
  Comparator #(.width(3)) comparator_1 (.a(3'b000), .b(Instruction[14:12]), .eq(func3_0));  // open: gt, lt
  Comparator #(.width(3)) comparator_2 (.a(3'b001), .b(Instruction[14:12]), .eq(func3_1));  // open: gt, lt
  Comparator #(.width(3)) comparator_3 (.a(3'b010), .b(Instruction[14:12]), .eq(func3_2));  // open: gt, lt
  Comparator #(.width(3)) comparator_4 (.a(3'b011), .b(Instruction[14:12]), .eq(func3_3));  // open: gt, lt
  Comparator #(.width(3)) comparator_5 (.a(3'b100), .b(Instruction[14:12]), .eq(func3_4));  // open: gt, lt
  Comparator #(.width(3)) comparator_6 (.a(3'b101), .b(Instruction[14:12]), .eq(func3_5));  // open: gt, lt
  Comparator #(.width(3)) comparator_7 (.a(3'b110), .b(Instruction[14:12]), .eq(func3_6));  // open: gt, lt
  Comparator #(.width(3)) comparator_8 (.a(3'b111), .b(Instruction[14:12]), .eq(func3_7));  // open: gt, lt
  Multiplexer #(.width(3), .enable("false")) multiplexer_3 (
    .in0(multiplexer_1_out), .in1(3'b001), .out(multiplexer_3_out), .sel(MemRw));
  Multiplexer #(.width(4), .enable("false")) multiplexer_4 (
    .in0(multiplexer_2_out), .in1(4'b0010), .out(multiplexer_4_out), .sel(or_4_out));
  Multiplexer #(.width(3), .enable("false")) multiplexer_5 (
    .in0(multiplexer_3_out), .in1(3'b010), .out(multiplexer_5_out), .sel(SB_type));
  Multiplexer #(.width(4), .enable("false")) multiplexer_6 (
    .in0(multiplexer_4_out), .in1(4'b0011), .out(multiplexer_6_out), .sel(or_8_out));
  or or_5 (BrUn, SB_bgeu, SB_bltu);
  or or_6 (or_6_out, and_1_out, and_2_out, and_3_out, and_4_out, and_5_out);
  Multiplexer #(.width(3), .enable("false")) multiplexer_7 (
    .in0(multiplexer_5_out), .in1(3'b011), .out(multiplexer_7_out), .sel(or_7_out));
  or or_7 (or_7_out, U_lui, U_auipc);
  or or_8 (or_8_out, R_add, I_addi, I_load_type, MemRw, SB_type, U_auipc, UJ_jal, I_jalr, U_lui);
  Multiplexer #(.width(4), .enable("false")) multiplexer_8 (
    .in0(multiplexer_6_out), .in1(4'b0100), .out(multiplexer_8_out), .sel(R_sub));
  Comparator #(.width(7)) comparator_9 (.a({7{1'b0}}), .b(Instruction[31:25]), .eq(func7_00));  // open: gt, lt
  Comparator #(.width(7)) comparator_10 (.a(7'b0000001), .b(Instruction[31:25]), .eq(func7_01));  // open: gt, lt
  Comparator #(.width(7)) comparator_11 (.a(7'b0100000), .b(Instruction[31:25]), .eq(func7_20));  // open: gt, lt
  or or_9 (PCSel, UJ_jal, or_6_out, I_jalr);
  Multiplexer #(.width(3), .enable("false")) multiplexer_9 (
    .in0(multiplexer_7_out), .in1(3'b100), .out(ImmSel), .sel(UJ_jal));
  Multiplexer #(.width(4), .enable("false")) multiplexer_10 (
    .in0(multiplexer_8_out), .in1(4'b0101), .out(multiplexer_10_out), .sel(R_mul));
  Comparator #(.width(7)) comparator_12 (.a(7'b0110011), .b(Instruction[6:0]), .eq(R_type));  // open: gt, lt
  Comparator #(.width(7)) comparator_13 (.a(7'b0000011), .b(Instruction[6:0]), .eq(I_load_type));  // open: gt, lt
  Multiplexer #(.width(4), .enable("false")) multiplexer_11 (
    .in0(multiplexer_10_out), .in1(4'b0110), .out(multiplexer_11_out), .sel(R_mulhu));
  Multiplexer #(.width(4), .enable("false")) multiplexer_12 (
    .in0(multiplexer_11_out), .in1(4'b0111), .out(multiplexer_12_out), .sel(R_mulh));
  Multiplexer #(.width(4), .enable("false")) multiplexer_13 (
    .in0(multiplexer_12_out), .in1(4'b1000), .out(multiplexer_13_out), .sel(R_divu));
  Multiplexer #(.width(2), .enable("false")) multiplexer_14 (
    .in0(2'b01), .in1(2'b00), .out(multiplexer_14_out), .sel(I_load_type));
  Multiplexer #(.width(4), .enable("false")) multiplexer_15 (
    .in0(multiplexer_13_out), .in1(4'b1001), .out(multiplexer_15_out), .sel(R_div));
  Comparator #(.width(7)) comparator_14 (.a(7'b0010011), .b(Instruction[6:0]), .eq(I_imm_type));  // open: gt, lt
  Comparator #(.width(7)) comparator_15 (.a(7'b0100011), .b(Instruction[6:0]), .eq(MemRw));  // open: gt, lt
  Comparator #(.width(7)) comparator_16 (.a(7'b1100011), .b(Instruction[6:0]), .eq(SB_type));  // open: gt, lt
  and and_6 (R_add, R_type, func3_0, func7_00);
  and and_7 (R_mul, R_type, func3_0, func7_01);
  and and_8 (R_sub, R_type, func3_0, func7_20);
  and and_9 (R_sll, R_type, func3_1, func7_00);
  and and_10 (I_addi, I_imm_type, func3_0);
  and and_11 (I_slli, I_imm_type, func3_1, func7_00);
  and and_12 (I_slti, I_imm_type, func3_2);
  and and_13 (S_sw, MemRw, func3_2);
  and and_14 (SB_bltu, SB_type, func3_6);
  or or_10 (or_10_out, MemRw, SB_type);
  not not_3 (RegWEn, or_10_out);
  Multiplexer #(.width(2), .enable("false")) multiplexer_16 (
    .in0(multiplexer_14_out), .in1(2'b10), .out(WBSel), .sel(or_11_out));
  or or_11 (or_11_out, I_jalr, UJ_jal);
  Multiplexer #(.width(4), .enable("false")) multiplexer_17 (
    .in0(multiplexer_15_out), .in1(4'b1010), .out(multiplexer_17_out), .sel(R_remu));
  or or_12 (or_12_out, I_srli, R_srl);
  Multiplexer #(.width(4), .enable("false")) multiplexer_18 (
    .in0(multiplexer_17_out), .in1(4'b1011), .out(multiplexer_18_out), .sel(or_12_out));
  Multiplexer #(.width(4), .enable("false")) multiplexer_19 (
    .in0(multiplexer_18_out), .in1(4'b1101), .out(multiplexer_19_out), .sel(I_slti));
  or or_13 (or_13_out, SB_type, UJ_jal, U_auipc);
  Multiplexer #(.width(3), .enable("false")) multiplexer_20 (
    .in0(3'b101), .in1(3'b000), .out(multiplexer_20_out), .sel(I_lb));
  Multiplexer #(.width(4), .enable("false")) multiplexer_21 (
    .in0(multiplexer_19_out), .in1(4'b1111), .out(Alu_Sel), .sel(or_14_out));
  or or_14 (or_14_out, R_sll, I_slli);
  Comparator #(.width(7)) comparator_17 (.a(7'b0010111), .b(Instruction[6:0]), .eq(U_auipc));  // open: gt, lt
  Comparator #(.width(7)) comparator_18 (.a(7'b0110111), .b(Instruction[6:0]), .eq(U_lui));  // open: gt, lt
  Comparator #(.width(7)) comparator_19 (.a(7'b1101111), .b(Instruction[6:0]), .eq(UJ_jal));  // open: gt, lt
  and and_15 (R_mulh, R_type, func3_1, func7_01);
  and and_16 (R_mulhu, R_type, func3_3, func7_01);
  and and_17 (R_xor, R_type, func3_4, func7_00);
  and and_18 (R_div, R_type, func3_4, func7_01);
  not not_4 (B_Sel, R_type);
  Multiplexer #(.width(2), .enable("false")) multiplexer_22 (
    .in0(2'b00), .in1(2'b01), .out(multiplexer_22_out), .sel(or_13_out));
  Multiplexer #(.width(3), .enable("false")) multiplexer_23 (
    .in0(multiplexer_20_out), .in1(3'b001), .out(multiplexer_23_out), .sel(I_lh));
  and and_19 (I_xori, I_imm_type, func3_4);
  and and_20 (I_srli, I_imm_type, func3_5, func7_00);
  and and_21 (I_ori, I_imm_type, func3_6);
  and and_22 (SB_beq, SB_type, func3_0);
  and and_23 (SB_bne, SB_type, func3_1);
  Multiplexer #(.width(2), .enable("false")) multiplexer_24 (
    .in0(multiplexer_22_out), .in1(2'b10), .out(A_Sel), .sel(U_lui));
  Multiplexer #(.width(3), .enable("false")) multiplexer_25 (
    .in0(multiplexer_23_out), .in1(3'b010), .out(multiplexer_25_out), .sel(I_lw));
  Multiplexer #(.width(3), .enable("false")) multiplexer_26 (
    .in0(multiplexer_25_out), .in1(3'b011), .out(multiplexer_26_out), .sel(I_lbu));
  Multiplexer #(.width(3), .enable("false")) multiplexer_27 (
    .in0(multiplexer_26_out), .in1(3'b100), .out(Mem_Read_Sel), .sel(I_lhu));
  and and_24 (R_divu, R_type, func3_5, func7_01);
  and and_25 (R_srl, R_type, func3_5, func7_00);
  and and_26 (R_or, R_type, func3_6, func7_00);
  and and_27 (R_remu, R_type, func3_7, func7_01);
  Comparator #(.width(7)) comparator_20 (.a(7'b1100111), .b(Instruction[6:0]), .eq(I_jalr));  // open: gt, lt
  and and_28 (SB_blt, SB_type, func3_4);
  and and_29 (SB_bgeu, SB_type, func3_7);
  and and_30 (R_and, R_type, func3_7, func7_00);
  and and_31 (I_lb, I_load_type, func3_0);
  and and_32 (I_lh, I_load_type, func3_1);
  and and_33 (I_lw, I_load_type, func3_2);
  and and_34 (I_lbu, I_load_type, func3_4);
  and and_35 (I_lhu, I_load_type, func3_5);
  and and_36 (I_andi, I_imm_type, func3_7);

  // Other names for the same wires on the sheet: Opcode[6:0] = Instruction[6:0]; func3[2:0] = Instruction[14:12];
  //   func7[6:0] = Instruction[31:25]; S_type = MemRw

  // Notes on the sheet:
  //   Input
  //   PCSel
  //   ImmSel
  //   BrUn
  //   MemRw
  //   RegWEn
  //   WBSel
  //   Alu_Sel
  //   B_Sel
  //   Mem_read_sel
  //   Instruction Decode
  //   Type Decode
  //   A_Sel
  //   Output
endmodule
