// Logisim project mem.circ as structural Verilog: 1 circuit, main circuit main
module main (
  input  [31:0] Address,
  input  Write_en,
  input  clk,
  input  [31:0] Write_data,
  output [31:0] Read_data
);

  RAM #(.addrWidth(24), .dataWidth(32), .trigger("falling"), .databus("bibus")) ram_1 (
    .addr(Address[23:0]), .we(Write_en), .oe(1'b1), .clk(clk), .din(Write_data), .dout(Read_data));
endmodule
